// Digital circuit HW1_2-Bit_Multiplier.dig as structural Verilog
module HW1_2_Bit_Multiplier (
  input  [1:0] A,
  input  [1:0] B,
  input  [1:0] A_2,
  input  [1:0] B_2,
  input  [1:0] A_3,
  input  [1:0] B_3,
  input  [1:0] in_9,
  input  [1:0] in_10,
  output P0,
  output P1,
  output P3,
  output P2
);

  wire and_2_out, and_4_out, and_5_out, and_6_out, and_7_out, and_8_out, not_2_out, not_3_out, not_4_out,
       not_5_out, not_6_out;

  and and_1 (P0, A_2[0], B_2[0]);
  not not_1 (A_3[0], B_3[0]);
  not not_2 (not_2_out, B_3[1]);
  not not_3 (not_3_out, B[0]);
  not not_4 (not_4_out, A_3[1]);
  not not_5 (not_5_out, A[0]);
  and and_2 (and_2_out, A[1], B[1], not_3_out);
  and and_3 (P3, in_9[0], in_9[1], in_10[0], in_10[1]);
  not not_6 (not_6_out, A_3[0]);
  and and_4 (and_4_out, not_6_out, A_3[1], B_3[0]);
  and and_5 (and_5_out, A_3[1], not_2_out, B_3[0]);
  and and_6 (and_6_out, not_4_out, A_3[0], B_3[1]);
  and and_7 (and_7_out, A_3[0], B_3[1], A_3[0]);
  and and_8 (and_8_out, A[1], not_5_out);  // open: In_2
  or or_1 (P2, and_2_out, and_8_out);
  or or_2 (P1, and_4_out, and_5_out, and_6_out, and_7_out);
  // Pins of 1 and 2 bits meet at A
  // Pins of 1 and 2 bits meet at B
  // Pins of 1 and 2 bits meet at A_2
  // Pins of 1 and 2 bits meet at B_2
  // Pins of 1 and 2 bits meet at A_3
  // Pins of 1 and 2 bits meet at B_3
  // Pins of 1 and 2 bits meet at in_9
  // Pins of 1 and 2 bits meet at in_10
endmodule
