// Digital circuit HW1_4-Bit_Carry_Adder.dig as structural Verilog
module HW1_4_Bit_Carry_Adder (
  input  Cin,
  input  B0,
  input  A0,
  input  B1,
  input  A1,
  input  B2,
  input  A2,
  input  B3,
  input  A3,
  output S0,
  output S1,
  output S2,
  output S3,
  output Cout
);

  wire _1_bit_full_adder_1_p3, _1_bit_full_adder_2_p3, _1_bit_full_adder_3_p3;

  // _1_Bit_Full_Adder _1_bit_full_adder_1: pin names not known; wires that end beside it: A3, B3, _1_bit_full_adder_1_p3, S3, Cout
  // _1_Bit_Full_Adder _1_bit_full_adder_2: pin names not known; wires that end beside it: A2, B2, _1_bit_full_adder_2_p3, S2, _1_bit_full_adder_1_p3
  // _1_Bit_Full_Adder _1_bit_full_adder_3: pin names not known; wires that end beside it: A1, B1, _1_bit_full_adder_3_p3, S1, _1_bit_full_adder_2_p3
  // _1_Bit_Full_Adder _1_bit_full_adder_4: pin names not known; wires that end beside it: A0, B0, Cin, S0, _1_bit_full_adder_3_p3
endmodule
