// Digital circuit HW1_Full_Adder.dig as structural Verilog
module HW1_Full_Adder (
  input  A,
  input  B,
  input  C,
  output SUM,
  output Cout
);

  wire and_1_out, and_2_out, and_3_out, xor_1_out;

  xor xor_1 (xor_1_out, A, B);
  and and_1 (and_1_out, A, B);
  and and_2 (and_2_out, B, C);
  and and_3 (and_3_out, A, C);
  xor xor_2 (SUM, xor_1_out, C);
  or or_1 (Cout, and_1_out, and_2_out, and_3_out);
endmodule
